// Logisim project Digital Vending Machine.circ as structural Verilog: 4 circuits, main circuit Digital Vending Machine
module Digital_Vending_Machine (
);

  wire _1_out, _2_out, _5_out, _10_out, Cancel_out, insert_money_1_out_6, insert_money_1_out_7,
       insert_money_1_out_8, insert_money_1_out_9, n4_bit_binary_to_7_segment_display_1_out_5,
       n4_bit_binary_to_7_segment_display_1_out_6, n4_bit_binary_to_7_segment_display_1_out_7,
       n4_bit_binary_to_7_segment_display_1_out_8, n4_bit_binary_to_7_segment_display_1_out_9,
       n4_bit_binary_to_7_segment_display_1_out_10, n4_bit_binary_to_7_segment_display_1_out_11,
       n4_bit_binary_to_7_segment_display_1_out_12, n4_bit_binary_to_7_segment_display_1_out_13,
       n4_bit_binary_to_7_segment_display_1_out_14, n4_bit_binary_to_7_segment_display_1_out_15,
       n4_bit_binary_to_7_segment_display_1_out_16, n4_bit_binary_to_7_segment_display_1_out_17,
       n4_bit_binary_to_7_segment_display_1_out_18;

  Button _1 (.out(_1_out));
  Button _2 (.out(_2_out));
  Button _5 (.out(_5_out));
  Button _10 (.out(_10_out));
  Button Cancel (.out(Cancel_out));
  Insert_Money insert_money_1 (
    ._1(_1_out), ._2(_2_out), ._5(_5_out), ._10(_10_out), .out_6(insert_money_1_out_6),
    .out_7(insert_money_1_out_7), .out_8(insert_money_1_out_8), .out_9(insert_money_1_out_9),
    .Clear(Cancel_out));
  _4_bit_binary_to_7_segment_display u_4_bit_binary_to_7_segment_display_1 (
    .in_1(insert_money_1_out_6), .in_2(insert_money_1_out_7), .in_3(insert_money_1_out_8),
    .in_4(insert_money_1_out_9), .out_5(n4_bit_binary_to_7_segment_display_1_out_5),
    .out_6(n4_bit_binary_to_7_segment_display_1_out_6), .out_7(n4_bit_binary_to_7_segment_display_1_out_7),
    .out_8(n4_bit_binary_to_7_segment_display_1_out_8), .out_9(n4_bit_binary_to_7_segment_display_1_out_9),
    .out_10(n4_bit_binary_to_7_segment_display_1_out_10),
    .out_11(n4_bit_binary_to_7_segment_display_1_out_11),
    .out_12(n4_bit_binary_to_7_segment_display_1_out_12),
    .out_13(n4_bit_binary_to_7_segment_display_1_out_13),
    .out_14(n4_bit_binary_to_7_segment_display_1_out_14),
    .out_15(n4_bit_binary_to_7_segment_display_1_out_15),
    .out_16(n4_bit_binary_to_7_segment_display_1_out_16),
    .out_17(n4_bit_binary_to_7_segment_display_1_out_17), .out_18(n4_bit_binary_to_7_segment_display_1_out_18));
  _7_Segment_Display u_7_segment_display_1 (
    .g(n4_bit_binary_to_7_segment_display_1_out_11), .f(n4_bit_binary_to_7_segment_display_1_out_10),
    .a(n4_bit_binary_to_7_segment_display_1_out_5), .b(n4_bit_binary_to_7_segment_display_1_out_6),
    .e(n4_bit_binary_to_7_segment_display_1_out_9), .d(n4_bit_binary_to_7_segment_display_1_out_8),
    .c(n4_bit_binary_to_7_segment_display_1_out_7));  // open: dp
  _7_Segment_Display u_7_segment_display_2 (
    .g(n4_bit_binary_to_7_segment_display_1_out_18), .f(n4_bit_binary_to_7_segment_display_1_out_17),
    .a(n4_bit_binary_to_7_segment_display_1_out_12), .b(n4_bit_binary_to_7_segment_display_1_out_13),
    .e(n4_bit_binary_to_7_segment_display_1_out_16), .d(n4_bit_binary_to_7_segment_display_1_out_15),
    .c(n4_bit_binary_to_7_segment_display_1_out_14));  // open: dp
endmodule

module Insert_Money (
  input  Clear,
  input  _1,
  input  _2,
  input  _5,
  input  _10,
  output out_6,
  output out_7,
  output out_8,
  output out_9
);

  wire adder_1_cout, adder_1_out, adder_2_cout, adder_2_out, adder_3_cout, adder_3_out, adder_4_cout,
       adder_4_out, LSB_out, nor_1_out, or_1_out;

  or or_1 (or_1_out, _10, _2);
  or LSB (LSB_out, _5, _1);
  nor nor_1 (nor_1_out, adder_1_cout, _10, _5, _2, _1);
  Adder #(.width(1)) adder_1 (.a(out_6), .b(_10), .out(adder_1_out), .cin(adder_2_cout), .cout(adder_1_cout));
  Adder #(.width(1)) adder_2 (.a(out_7), .b(_5), .out(adder_2_out), .cin(adder_3_cout), .cout(adder_2_cout));
  Adder #(.width(1)) adder_3 (.a(out_8), .b(or_1_out), .out(adder_3_out), .cin(adder_4_cout), .cout(adder_3_cout));
  Adder #(.width(1)) adder_4 (.a(out_9), .b(LSB_out), .out(adder_4_out), .cout(adder_4_cout));  // open: cin
  D_Flip_Flop d_ff_1 (.clk(nor_1_out), .D(adder_1_out), .Q(out_6), .reset(Clear));  // open: Qn, preset, en
  D_Flip_Flop d_ff_2 (.clk(nor_1_out), .D(adder_2_out), .Q(out_7), .reset(Clear));  // open: Qn, preset, en
  D_Flip_Flop d_ff_3 (.clk(nor_1_out), .D(adder_3_out), .Q(out_8), .reset(Clear));  // open: Qn, preset, en
  D_Flip_Flop d_ff_4 (.clk(nor_1_out), .D(adder_4_out), .Q(out_9), .reset(Clear));  // open: Qn, preset, en
endmodule

module _4_bit_binary_to_7_segment_display (
  input  in_1,
  input  in_2,
  input  in_3,
  input  in_4,
  output out_5,
  output out_6,
  output out_7,
  output out_8,
  output out_9,
  output out_10,
  output out_11,
  output out_12,
  output out_13,
  output out_14,
  output out_15,
  output out_16,
  output out_17,
  output out_18
);

  wire _0_out, _1_out, _2_out, _3_out, _4_out, _5_out, _6_out, _7_out, _8_out, _10_out, _11_out, _12_out,
       _13_out, _14_out, _15_out, not_1_out, not_2_out, not_3_out, not_4_out;

  not not_1 (not_1_out, in_1);
  not not_2 (not_2_out, in_2);
  not not_3 (not_3_out, in_3);
  not not_4 (not_4_out, in_4);
  and _0 (_0_out, not_1_out, not_2_out, not_3_out, not_4_out);
  and _1 (_1_out, not_1_out, not_2_out, not_3_out, in_4);
  and _2 (_2_out, not_1_out, not_2_out, in_3, not_4_out);
  and _3 (_3_out, not_1_out, not_2_out, in_3, in_4);
  and _5 (_5_out, not_1_out, in_2, not_3_out, in_4);
  and _4 (_4_out, not_1_out, in_2, not_3_out, not_4_out);
  and _6 (_6_out, not_1_out, in_2, in_3, not_4_out);
  and _7 (_7_out, not_1_out, in_2, in_3, in_4);
  // AND_Gate _9 has open pins: in0=in_1, in1=not_2_out, in2=not_3_out, in3=in_4, out=open
  and _8 (_8_out, in_1, not_2_out, not_3_out, not_4_out);
  and _10 (_10_out, in_1, not_2_out, in_3, not_4_out);
  and _11 (_11_out, in_1, not_2_out, in_3, in_4);
  and _12 (_12_out, in_1, in_2, not_3_out, not_4_out);
  and _13 (_13_out, in_1, in_2, not_3_out, in_4);
  and _14 (_14_out, in_1, in_2, in_3, not_4_out);
  and _15 (_15_out, in_1, in_2, in_3, in_4);
  or or_1 (out_16, _12_out, _10_out, _8_out, _6_out, _2_out, _0_out);
  nor nor_1 (out_5, _15_out, _14_out, _13_out, _12_out, _11_out, _10_out);
  nor nor_2 (out_12, _14_out, _11_out, _4_out, _1_out);
  nor nor_3 (out_13, _15_out, _6_out, _5_out);
  nor nor_4 (out_14, _12_out, _2_out);
  nor nor_5 (out_15, _14_out, _11_out, _7_out, _4_out, _1_out);
  nor nor_6 (out_17, _13_out, _12_out, _11_out, _7_out, _3_out, _2_out, _1_out);
  nor nor_7 (out_18, _11_out, _10_out, _7_out, _1_out, _0_out);

  assign out_6 = 1'b1;
  assign out_7 = 1'b1;
  assign out_8 = out_5;
  assign out_9 = out_5;
  assign out_10 = out_5;
  assign out_11 = 1'b0;
endmodule

module Profuct_Selection (
  input  _1,
  input  _2,
  input  _10,
  input  _25,
  input  _60
);

  wire LSB_out, or_1_out, or_2_out, or_3_out;

  // OR_Gate or_1 has open pins: out=or_1_out
  // OR_Gate or_2 has open pins: out=or_2_out
  // OR_Gate or_3 has open pins: out=or_3_out
  // OR_Gate LSB has open pins: out=LSB_out
endmodule
